# Fritzing sketch tv-remote (saved by Fritzing 0.9.3b)
circuit board: 5.90248cm x 4.56479cm
breadboards: 1

parts:
  Part1 = Adafruit HUZZAH ESP8266 [part_number="Adafruit #2471"]
  Transistor = PNP-Transistor [package="TO92 [THT]"]
  J1 = double row female pin header, 4 pins [form="♀ (female)"]
  Res = Resistor [tolerance=±5% resistance=220 package=THT]
  IR_Tx = LED - 3mm [color="Red (633nm)" package="3 mm [THT]"]

nets (from the pcb view):
  N1: Part1.GND, J1.pin3, J1.pin4, Res.Pin_0
  N2: Part1.VBAT, J1.pin1, J1.pin2
  N3: Part1.3.3V, IR_Tx.cathode
  N4: Part1.GPIO4, Transistor.C
  N5: Transistor.E, Res.Pin_1
  N6: Transistor.B, IR_Tx.anode

notes:
  SJR

custom parts:
  Adafruit HUZZAH ESP8266: Add Internet to your next project with an adorable, bite-sized WiFi microcontroller, at a price you like! The ESP8266 processor from Espressif is an 80 MHz microcontroller with a full WiFi front-end (both as client and access point) and TCP/IP stack with DNS support as well. While this chip has been very popular, its also been very difficult to use. Most of the low cost modules are not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
